# Fritzing sketch 360Timelapse_forSchematic_v2 (saved by Fritzing 0.9.3b)
circuit board: 4.99822cm x 3.24308cm
breadboards: 1

parts:
  R6_led10 = Resistor [tolerance=±5% resistance=220 package=THT]
  BAT1 = Battery Holders [package=battery-aa-kit]
  Power_sw1 = Dagu DGServo 9g header (male) [package=THT]
  J1 = female pin header, 1 pin [form="♀ (female)"]
  ATmega8 = MICROCONTROLLER [package=dil28-3-simon]
  R6_led9 = Resistor [tolerance=±5% resistance=220 package=THT]
  Pad1 = Pad [width=5.4494743436070356 height=4.8341311529477897 connect=center]  # not connected
  R6_led11 = Resistor [tolerance=±5% resistance=220 package=THT]
  R6_led8 = Resistor [tolerance=±5% resistance=220 package=THT]
  Pad2 = Pad [width=5.7999999999999998 height=4.7258681977788832 connect=center]  # not connected
  M1 = Header 4 [package=molex-1x4_lock]
  R6_led12 = Resistor [tolerance=±5% resistance=220 package=THT]
  LED1 = LED - 3mm [color="Red (633nm)" package="3 mm [THT]"]
  S1 = Pushbutton [package=THT]
  S2 = Pushbutton [package=THT]
  LED2 = LED - 3mm [color="Red (633nm)" package="3 mm [THT]"]
  LED3 = LED - 3mm [color="Red (633nm)" package="3 mm [THT]"]
  R6_led13 = Resistor [tolerance=±5% resistance=220 package=THT]
  S3 = Pushbutton [package=THT]
  S4 = Pushbutton [package=THT]
  LED4 = LED - 3mm [color="Red (633nm)" package="3 mm [THT]"]
  LED5 = LED - 3mm [color="Red (633nm)" package="3 mm [THT]"]
  LED6 = LED - 3mm [color="Red (633nm)" package="3 mm [THT]"]
  R6_led14 = Resistor [tolerance=±5% resistance=220 package=THT]
  U1 = SWITCH_SPDT [package=kps-1290]

nets:
  N1: R6_led10.Pin_0, ATmega8.PB0(ICP), S1.leg1
  N2: R6_led10.Pin_1, ATmega8.VCC, R6_led9.Pin_1, R6_led11.Pin_1, R6_led8.Pin_1, R6_led12.Pin_1, R6_led13.Pin_0, R6_led14.Pin_0, U1.S
  N3: BAT1.+, U1.P
  N4: BAT1.-, ATmega8.AGND
  N5: Power_sw1.gnd, ATmega8.PB5(SCK)
  N6: Power_sw1.Vcc, ATmega8.PB4(MISO)
  N7: Power_sw1.pulse, ATmega8.PB3(MOSI_OC2)
  N8: J1.pin1, ATmega8.PC6(_RESET)
  N9: ATmega8.PD0(RXD), R6_led9.Pin_0, S4.leg1
  N10: ATmega8.PD1(TXD), R6_led8.Pin_0, S3.leg1
  N11: ATmega8.PD2(INT0), LED6.cathode
  N12: ATmega8.PD3(INT1), LED5.cathode
  N13: ATmega8.PD4(XCK_T0), LED4.cathode
  N14: ATmega8.GND, LED1.cathode, S1.leg0, S2.leg0, S3.leg0, S4.leg0
  N15: ATmega8.PD5(T1), LED3.cathode
  N16: ATmega8.PD6(AIN0), LED2.cathode
  N17: ATmega8.PD7(AIN1), R6_led11.Pin_0, S2.leg1
  N18: ATmega8.AVCC, ATmega8.AREF
  N19: ATmega8.PC2(ADC2), M1.4
  N20: ATmega8.PC3(ADC3), M1.3
  N21: ATmega8.PC4(ADC4_SDA), M1.2
  N22: ATmega8.PC5(ADC5_SCL), M1.1
  N23: R6_led12.Pin_0, LED1.anode
  N24: LED2.anode, LED3.anode, R6_led13.Pin_1
  N25: LED4.anode, LED5.anode, LED6.anode, R6_led14.Pin_1
